# Fritzing sketch TempDCMOTOR (saved by Fritzing 0.9.9b)
breadboards: 1

parts:
  Part1 = Arduino Uno (Rev3)
  T1 = LM34 Temperature Sensor [package="TO92 [THT]"]
  U1 = TRANSISTOR_NPN_2 [package=to-92]
  R1 = Resistor [tolerance=±5% power=0.25 resistance=220 package=THT]
  D1 = Rectifier Diode [part_number=1N4001 package="300 mil [THT]"]
  M1 = DC Motor

nets:
  N1: Part1.A0, T1.Vout
  N2: Part1.D9_PWM, R1.Pin_1
  N3: Part1.5V, D1.cathode, M1.pin_2
  GND: Part1.GND, T1.+Vs, T1.GND, U1.E
  N4: U1.C, D1.anode, M1.pin_1
  N5: U1.B, R1.Pin_0
